# Fritzing sketch connection (saved by Fritzing 0.9.3b)
breadboards: 1

parts:
  U1 = ESP32S-HiLetgo [part_number=ESP32S-HiLetgo]
  VCC1 = Battery  # not connected
  VCC2 = Battery  # not connected
  DC1 = DC_DC_XL4016 [chip_label=XL4016 package=board_screw]  # not connected
  U2 = LM2596 step down module
  J1 = Basic Servo
  J2 = Basic Servo
  J3 = Basic Servo
  J4 = Basic Servo
  J5 = Basic Servo
  S1 = Square Pushbutton
  IC1 = Voltage Regulator [package=to220-igo]
  J6 = Basic Servo

nets:
  GND: U1.GND, U2.OUT-, J1.gnd, J2.gnd, J3.gnd, J4.gnd, J5.gnd, IC1.GND, J6.gnd
  N1: U1.VIN, IC1.OUT
  N2: U2.IN+, S1.leg1
  VCC: U2.OUT+, J1.vcc, J2.vcc, J3.vcc, J4.vcc, J5.vcc, IC1.IN, J6.vcc

custom parts:
  ESP32S-HiLetgo: HiLetgo ESP-WROOM-32 ESP32 ESP-32S Development Board 2.4GHz Dual-Mode WiFi + Bluetooth Dual Cores Microcontroller The ESP32 integrated with Antenna switches, RF Balun, power amplifiers, low-noise amplifiers, filters, and management modules, and the entire solution occupies the least area of PCB. 2.4 GHz Wi-Fi plus Bluetooth dual-mode chip, with TSMC Ultra-low power consumption 40nm technology,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
  DC_DC_XL4016: DC-DC Converter step down voltage regulator XL4016 custom sketch.
  LM2596 step down module: LM2596 DC-DC step down power supply module 3 A.
